# Fritzing sketch Uno_radioFeatherwing (saved by Fritzing 0.9.3b)

parts:
  Composant6 = Adafruit Radio FeatherWing [part_number="Adafruit #3229, 3230, 3231, 3232"]
  Composant7 = Arduino Uno (Rev3)

nets:
  N1: Composant6.IRQ, Composant6.C, Composant7.D2
  N2: Composant6.CS, Composant6.B, Composant7.D10_PWM/SS
  N3: Composant6.RF_RST, Composant6.A, Composant7.D9_PWM
  3.3V: Composant6.3.3V, Composant7.3V3
  GND: Composant6.GND, Composant7.GND
  N4: Composant6.SCK, Composant7.D13/SCK
  N5: Composant6.MOSI, Composant7.D11_PWM/MOSI
  N6: Composant6.MISO, Composant7.D12/MISO

custom parts:
  Adafruit Radio FeatherWing: Add short-hop wireless to your Feather with these Radio Featherwings. These add-ons for any Feather board will let you integrate packetized radio (with the RFM69 radio) or LoRa radio (with the RFM9x's). These radios are good options for kilometer-range radio, and paired with one of our WiFi, cellular or Bluetooth Feathers, will let you bridge from 433/900 MHz to the Internet or your mobile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
